# Fritzing sketch catapult-button-edison (saved by Fritzing 0.9.3b)
breadboards: 1

parts:
  Part1 = Intel Edison Arduinobreakout
  J1 = Basic Servo
  S1 = Pushbutton [package="[SMD]"]
  R1 = Resistor [tolerance=±5% resistance=220 package="2010 [SMD]"]

nets:
  N1: Part1.D13/SCK, S1.Pin_3, S1.Pin_4, R1.Pin_1
  GND: Part1.GND, J1.gnd, S1.Pin_1, S1.Pin_2
  N2: Part1.D6_PWM, J1.pulse
  5V: Part1.5V, J1.vcc, R1.Pin_0
