# Fritzing sketch catapult-button-raspberry (saved by Fritzing 0.9.3b)
breadboards: 1

parts:
  J1 = Basic Servo
  S1 = Pushbutton [package="[SMD]"]
  R1 = Resistor [tolerance=±5% resistance=220 package="2010 [SMD]"]
  Raspberry_Pi_1 = Raspberry Pi 3 [part_number=RPI-3-V1.2]

nets:
  GND: J1.gnd, S1.Pin_1, S1.Pin_2, Raspberry_Pi_1.GND
  VCC: J1.vcc, R1.Pin_0, Raspberry_Pi_1.5V
  N1: J1.pulse, Raspberry_Pi_1.GPIO18
  N2: S1.Pin_3, S1.Pin_4, R1.Pin_1, Raspberry_Pi_1.GPIO17
